// Logisim project 19_Moving Sign.circ as structural Verilog: 1 circuit, main circuit main
module main (
);

  wire clock_1_out, d_ff_2_q, d_ff_2_qn, d_ff_3_q, d_ff_3_qn, d_ff_4_q, d_ff_4_qn, d_ff_5_q, d_ff_5_qn,
       undriven;

  LED led_1 ();  // open: in
  Clock clock_1 (.out(clock_1_out));
  LED led_2 ();  // open: in
  LED led_3 ();  // open: in
  D_Flip_Flop d_ff_1 (.clk(clock_1_out), .D(undriven), .preset(1'b0), .reset(1'b0));  // open: Q, Qn, en
  LED led_4 ();  // open: in
  LED led_5 ();  // open: in
  LED led_6 ();  // open: in
  D_Flip_Flop d_ff_2 (.D(d_ff_2_qn), .Q(d_ff_2_q), .Qn(d_ff_2_qn), .preset(1'b0), .reset(1'b0));  // open: clk, en
  LED led_7 ();  // open: in
  LED led_8 ();  // open: in
  LED led_9 ();  // open: in
  D_Flip_Flop d_ff_3 (
    .clk(d_ff_2_q), .D(d_ff_3_qn), .Q(d_ff_3_q), .Qn(d_ff_3_qn), .preset(1'b0), .reset(1'b0));  // open: en
  LED led_10 ();  // open: in
  LED led_11 ();  // open: in
  D_Flip_Flop d_ff_4 (
    .clk(d_ff_3_q), .D(d_ff_4_qn), .Q(d_ff_4_q), .Qn(d_ff_4_qn), .preset(1'b0), .reset(1'b0));  // open: en
  LED led_12 ();  // open: in
  LED led_13 ();  // open: in
  LED led_14 ();  // open: in
  D_Flip_Flop d_ff_5 (
    .clk(d_ff_4_q), .D(d_ff_5_qn), .Q(d_ff_5_q), .Qn(d_ff_5_qn), .preset(1'b0), .reset(1'b0));  // open: en
  LED led_15 ();  // open: in
  LED led_16 ();  // open: in
  LED led_17 ();  // open: in
  LED led_18 ();  // open: in
  LED led_19 ();  // open: in
  LED led_20 ();  // open: in
  LED led_21 ();  // open: in
  LED led_22 ();  // open: in
  LED led_23 ();  // open: in
  LED led_24 ();  // open: in
  LED led_25 ();  // open: in
  LED led_26 ();  // open: in
  LED led_27 ();  // open: in
  LED led_28 ();  // open: in
  LED led_29 ();  // open: in
endmodule
